// Logisim project cpu.circ as structural Verilog: 2 circuits, main circuit main
module main (
);

  wire clock_1_out, decoder_1_out0, decoder_1_out1, decoder_1_out2, decoder_1_out3;
  wire [1:0] rom_1_data_2;
  wire [5:0] rom_1_data;
  wire [7:0] A_q, counter_1_q;

  Counter #(.trigger("falling")) counter_1 (
    .clk(clock_1_out), .Q(counter_1_q));  // open: clr, load, up, count, D, carry
  Clock clock_1 (.out(clock_1_out));
  ROM rom_1 (.addr(counter_1_q), .data({rom_1_data_2, rom_1_data}));
  Decoder #(.select(2)) decoder_1 (
    .out0(decoder_1_out0), .out1(decoder_1_out1), .out2(decoder_1_out2), .out3(decoder_1_out3),
    .sel(rom_1_data_2));  // open: en
  Register A (.D(A_q), .en(decoder_1_out0), .clk(clock_1_out), .Q(A_q));  // open: clr
  Register B (.D(A_q), .clk(clock_1_out), .Q(A_q));  // open: en, clr
  Register C (.D(A_q), .clk(clock_1_out), .Q(A_q));  // open: en, clr
  Register D (.D(A_q), .clk(clock_1_out), .Q(A_q));  // open: en, clr
  Register E (.D(A_q), .clk(clock_1_out), .Q(A_q));  // open: en, clr
  Register F (.D(A_q), .clk(clock_1_out), .Q(A_q));  // open: en, clr

  // Notes on the sheet:
  //   contents of rom_1 (hex, n*v repeats v):
  //   ff
  //   imm
  //   alu
  //   mov
  //   cond
endmodule

module ALU (
  input  [2:0] Op,
  input  [7:0] A,
  input  [7:0] B,
  output [7:0] Aout
);

  wire decoder_1_out0, decoder_1_out1, decoder_1_out2, decoder_1_out3, decoder_1_out4, decoder_1_out5;
  wire [7:0] adder_1_out, and_1_out, nand_1_out, nor_1_out, or_1_out, subtractor_1_out;

  Decoder #(.select(3)) decoder_1 (
    .out0(decoder_1_out0), .out1(decoder_1_out1), .out2(decoder_1_out2), .out3(decoder_1_out3),
    .out4(decoder_1_out4), .out5(decoder_1_out5), .sel(Op));  // open: out6, out7, en
  assign nand_1_out = ~(A & B);  // NAND_Gate nand_1, 8 bits wide
  assign Aout = decoder_1_out0 ? nand_1_out : 8'bz;  // Controlled_Buffer controlled_buffer_1
  assign or_1_out = B | A;  // OR_Gate or_1, 8 bits wide
  assign Aout = decoder_1_out1 ? or_1_out : 8'bz;  // Controlled_Buffer controlled_buffer_2
  assign and_1_out = B & A;  // AND_Gate and_1, 8 bits wide
  assign Aout = decoder_1_out2 ? and_1_out : 8'bz;  // Controlled_Buffer controlled_buffer_3
  assign nor_1_out = ~(B | A);  // NOR_Gate nor_1, 8 bits wide
  assign Aout = decoder_1_out3 ? nor_1_out : 8'bz;  // Controlled_Buffer controlled_buffer_4
  assign Aout = decoder_1_out4 ? adder_1_out : 8'bz;  // Controlled_Buffer controlled_buffer_5
  Adder adder_1 (.a(B), .b(A), .out(adder_1_out));  // open: cin, cout
  assign Aout = decoder_1_out5 ? subtractor_1_out : 8'bz;  // Controlled_Buffer controlled_buffer_6
  Subtractor subtractor_1 (.a(A), .b(B), .out(subtractor_1_out));  // open: bin, bout
endmodule
